// Logisim project tragamonedas.circ as structural Verilog: 5 circuits, main circuit main
module main (
  input  [1:0] in_1,
  input  [1:0] Resultados,
  input  [1:0] in_3,
  input  [1:0] in_4,
  output out_5
);

  wire clock_1_out, controlador_animacion_1_display_1, controlador_animacion_1_display_2,
       controlador_animacion_1_display_3, Controlador_Palanca_influye;
  wire [1:0] counter_1_q, counter_2_q, counter_3_q, joystick_1_y;
  wire [6:0] controlador_display_1_columna_1, controlador_display_1_columna_2,
       controlador_display_1_columna_3, controlador_display_1_columna_4, controlador_display_1_columna_5,
       controlador_display_2_columna_1, controlador_display_2_columna_2, controlador_display_2_columna_3,
       controlador_display_2_columna_4, controlador_display_2_columna_5, controlador_display_3_columna_1,
       controlador_display_3_columna_2, controlador_display_3_columna_3, controlador_display_3_columna_4,
       controlador_display_3_columna_5;

  DotMatrix dotmatrix_1 (
    .col0(controlador_display_1_columna_1), .col1(controlador_display_1_columna_2),
    .col2(controlador_display_1_columna_3), .col3(controlador_display_1_columna_4),
    .col4(controlador_display_1_columna_5));
  controlador_display controlador_display_1 (
    .Simbolo_animacion(counter_1_q), .Resultado(in_1), .Detener(controlador_animacion_1_display_1),
    .Columna_1(controlador_display_1_columna_1), .Columna_2(controlador_display_1_columna_2),
    .Columna_3(controlador_display_1_columna_3), .Columna_4(controlador_display_1_columna_4),
    .Columna_5(controlador_display_1_columna_5));
  Counter #(.width(2), .max('h2)) counter_1 (.Q(counter_1_q), .clk(clock_1_out));  // open: load, D, count, carry, clr
  // Probe on joystick_1_y
  Joystick #(.bits(2)) joystick_1 (.y(joystick_1_y));  // open: x
  DotMatrix dotmatrix_2 (
    .col0(controlador_display_2_columna_1), .col1(controlador_display_2_columna_2),
    .col2(controlador_display_2_columna_3), .col3(controlador_display_2_columna_4),
    .col4(controlador_display_2_columna_5));
  controlador_display controlador_display_2 (
    .Simbolo_animacion(counter_2_q), .Resultado(Resultados), .Detener(controlador_animacion_1_display_2),
    .Columna_1(controlador_display_2_columna_1), .Columna_2(controlador_display_2_columna_2),
    .Columna_3(controlador_display_2_columna_3), .Columna_4(controlador_display_2_columna_4),
    .Columna_5(controlador_display_2_columna_5));
  Counter #(.width(2), .max('h2)) counter_2 (.Q(counter_2_q), .clk(clock_1_out));  // open: load, D, count, carry, clr
  Clock clock_1 (.out(clock_1_out));
  controlador_palanca Controlador_Palanca (
    .Estado_de_Juego(in_4), .Palanca(joystick_1_y), .Influye(Controlador_Palanca_influye),
    .Activacion_Palanca(out_5));
  LED Influye (.in(Controlador_Palanca_influye));
  DotMatrix dotmatrix_3 (
    .col0(controlador_display_3_columna_1), .col1(controlador_display_3_columna_2),
    .col2(controlador_display_3_columna_3), .col3(controlador_display_3_columna_4),
    .col4(controlador_display_3_columna_5));
  controlador_display controlador_display_3 (
    .Simbolo_animacion(counter_3_q), .Resultado(in_3), .Detener(controlador_animacion_1_display_3),
    .Columna_1(controlador_display_3_columna_1), .Columna_2(controlador_display_3_columna_2),
    .Columna_3(controlador_display_3_columna_3), .Columna_4(controlador_display_3_columna_4),
    .Columna_5(controlador_display_3_columna_5));
  controlador_animacion controlador_animacion_1 (
    .Reloj(clock_1_out), .Palanca(out_5), .Display_1(controlador_animacion_1_display_1),
    .Display_2(controlador_animacion_1_display_2), .Display_3(controlador_animacion_1_display_3));
  Counter #(.width(2), .max('h2)) counter_3 (.Q(counter_3_q), .clk(clock_1_out));  // open: load, D, count, carry, clr
  LED \Detección_Palanca  (.in(out_5));

  // Notes on the sheet:
  //   Harcodeados
  //   Controlador
  //   Display
  //   Harcodeado estado 11 = estado espera
  //   Controlador
  //   Display
  //   Controlador
  //   Display
  //   Controlador
  //   Animacion
endmodule

module controlador_display (
  input  [1:0] Simbolo_animacion,
  input  [1:0] Resultado,
  input  Detener,
  output [6:0] Columna_1,
  output [6:0] Columna_2,
  output [6:0] Columna_3,
  output [6:0] Columna_4,
  output [6:0] Columna_5
);

  wire [1:0] multiplexer_1_out;

  Multiplexer #(.width(2), .enable("false")) multiplexer_1 (
    .in0(Simbolo_animacion), .in1(Resultado), .out(multiplexer_1_out), .sel(Detener));
  ROM #(.addrWidth(2), .dataWidth(7)) rom_1 (.addr(multiplexer_1_out), .data(Columna_1));  // open: sel
  ROM #(.addrWidth(2), .dataWidth(7)) rom_2 (.addr(multiplexer_1_out), .data(Columna_2));  // open: sel
  ROM #(.addrWidth(2), .dataWidth(7)) rom_3 (.addr(multiplexer_1_out), .data(Columna_3));  // open: sel
  ROM #(.addrWidth(2), .dataWidth(7)) rom_4 (.addr(multiplexer_1_out), .data(Columna_4));  // open: sel
  ROM #(.addrWidth(2), .dataWidth(7)) rom_5 (.addr(multiplexer_1_out), .data(Columna_5));  // open: sel

  // Notes on the sheet:
  //   contents of rom_1 (hex, n*v repeats v):
  //   40 6 8
  //   contents of rom_2 (hex, n*v repeats v):
  //   43 3e 1b
  //   contents of rom_3 (hex, n*v repeats v):
  //   4c 7f 3e
  //   contents of rom_4 (hex, n*v repeats v):
  //   58 3e 6c
  //   contents of rom_5 (hex, n*v repeats v):
  //   60 6 8
endmodule

module controlador_palanca (
  input  [1:0] Estado_de_Juego,
  input  [1:0] Palanca,
  output Influye,
  output Activacion_Palanca
);

  wire and_2_out;

  and and_1 (Influye, Estado_de_Juego[0], Estado_de_Juego[1]);
  and and_2 (and_2_out, Palanca[0], Palanca[1]);
  and and_3 (Activacion_Palanca, Influye, and_2_out);
endmodule

module controlador_animacion (
  input  Reloj,
  input  Palanca,
  output Display_1,
  output Display_2,
  output Display_3
);

  wire comparator_1_eq, comparator_1_gt, comparator_2_eq, comparator_2_gt, comparator_3_eq, comparator_3_gt;
  wire [2:0] counter_1_q;

  Counter #(.width(3), .max('h7), .ongoal("stay")) counter_1 (
    .Q(counter_1_q), .clk(Reloj), .clr(Palanca));  // open: load, D, count, carry
  Comparator #(.width(3), .mode("unsigned")) comparator_1 (
    .a(counter_1_q), .b(3'b101), .gt(comparator_1_gt), .eq(comparator_1_eq));  // open: lt
  Comparator #(.width(3), .mode("unsigned")) comparator_2 (
    .a(counter_1_q), .b(3'b110), .gt(comparator_2_gt), .eq(comparator_2_eq));  // open: lt
  Comparator #(.width(3), .mode("unsigned")) comparator_3 (
    .a(counter_1_q), .b(3'b111), .gt(comparator_3_gt), .eq(comparator_3_eq));  // open: lt
  or or_1 (Display_1, comparator_1_gt, comparator_1_eq);
  or or_2 (Display_2, comparator_2_gt, comparator_2_eq);
  or or_3 (Display_3, comparator_3_gt, comparator_3_eq);

  // Notes on the sheet:
  //   Tiempo
  //   Animacion
  //   Detener 1
  //   tiempo ≥ 5
  //   Detener 2
  //   tiempo ≥ 6
  //   Detener 3
endmodule

module generador_resultados (
  input  Generar,
  input  Reloj,
  output [1:0] out_3
);

  wire and_1_out, and_2_out, comparator_1_eq, not_1_out, not_2_out, or_1_out, register_1_q;
  wire [1:0] random_1_out;

  or or_1 (or_1_out, and_2_out, Generar);
  Register #(.width(1)) register_1 (.D(or_1_out), .en(1'b1), .Q(register_1_q), .clk(Reloj));  // open: clr
  not not_1 (not_1_out, Generar);
  Random #(.width(2), .seed(1)) random_1 (.clk(Reloj), .out(random_1_out));  // open: next, clr
  and and_1 (and_1_out, register_1_q, not_1_out, not_2_out);
  Comparator #(.width(2)) comparator_1 (.a(random_1_out), .b(2'b11), .eq(comparator_1_eq));  // open: gt, lt
  and and_2 (and_2_out, register_1_q, comparator_1_eq);
  not not_2 (not_2_out, comparator_1_eq);
  Register #(.width(2)) register_2 (.D(random_1_out), .en(and_1_out), .Q(out_3), .clk(Reloj));  // open: clr

  // Notes on the sheet:
  //   Buscando
  //   Generar
endmodule
